# Fritzing sketch arduino-brain-machine-mono (saved by Fritzing 0.9.2b)
breadboards: 1

parts:
  Part1 = Arduino Uno (Rev3) - ICSP
  J1 = Screw terminal - 2 pins [package=THT]
  Arduino_Power = Battery block 9V
  LED = LEDs [package=led10mm]
  R3 = Resistor [tolerance=±5% resistance=10k package="2512 [SMD]"]
  Phones_jack = TRRS 3.5mm Jack Breakout
  S1 = Momentary Switch [package=ksa_sealed_tac_switch]
  POT1 = POT [package=alps_pot]
  LED_N-Channel_FET = MOSFET-NCHANNEL [package=to220v]
  LED_power = Battery block 9V
  Audio_P-Channel_FET = Basic FET N-Channel [package="D2Pak [SMD]"]

nets:
  N1: Part1.A0, POT1.S
  N2: Part1.5V, POT1.E
  GND: Part1.GND, J1.pin2, Arduino_Power.-, Phones_jack.SLEEVE, S1.1, S1.2, POT1.A, LED_N-Channel_FET.S, LED_power.-
  N3: Part1.D10_PWM/SS, R3.Pin_1
  N4: Part1.D2, S1.3, S1.4
  N5: Part1.D5_PWM, Audio_P-Channel_FET.Gate
  N6: Part1.D6_PWM, LED_N-Channel_FET.G
  N7: Part1.VIN, J1.pin1, Arduino_Power.+
  N8: LED.A, LED_N-Channel_FET.D
  N9: LED.C, LED_power.+
  N10: R3.Pin_0, Audio_P-Channel_FET.source
  N11: Phones_jack.RING1, Phones_jack.TIP, Audio_P-Channel_FET.drain
